# Fritzing sketch 2WireMotorDriver (saved by Fritzing 0.9.2b)

parts:
  S1 = H-Bridge with L298N
  J2 = female pin header, 2 pins [form="♀ (female)"]
  Part1 = Arduino Pro Mini v13
  M1 = DC Motor
  Power_plug1 = Power plug

nets:
  12V: S1.12V, Power_plug1.VCC
  GND: S1.GND, Part1.GND, Power_plug1.GND
  5V: S1.5V, Part1.VCC
  N1: S1.ENA, J2.pin2
  N2: S1.IN1, Part1.D6_PWM
  N3: S1.IN2, Part1.D5_PWM
  N4: S1.M1-01, M1.pin_2
  N5: S1.M1-02, M1.pin_1
  N6: S1.ENA-5V, J2.pin1

custom parts:
  H-Bridge with L298N: h-bridge
